// Logisim project test.circ as structural Verilog: 1 circuit, main circuit main
module main (
);

  wire and_1_out, nand_1_out, not_1_out, or_1_out, undriven;

  buf and_1 (and_1_out, undriven);  // AND_Gate
  not not_1 (not_1_out, 1'b1);
  or or_1 (or_1_out, not_1_out, 1'b1);
  nand nand_1 (nand_1_out, 1'b1, or_1_out);
endmodule
